// Digital circuit 4bit_CPU.dig as structural Verilog
module _4bit_CPU (
  input  clk
);

  wire [0:0] register_1_q;
  wire [1:0] and_1_out, pc_1_p2;
  wire [3:0] alu_1_p4, IR_q, multiplexer_1_out, multiplexer_2_out, pc_1_p3, RAM_d, RF_rdata1, RF_rdata2;
  wire [8:0] CU_out;

  and and_1 (and_1_out[1], ~register_1_q[0], ~and_1_out[0]);  // And
  // PC pc_1: pin names not known; wires that end beside it: clk, pc_1_p2[0], pc_1_p3
  Register #(.Bits(2)) register_1 (.D(and_1_out), .C(clk), .en(1'b1), .Q({and_1_out[0], register_1_q[0]}));
  RAMDualPort #(.AddrBits(4), .isProgramMemory("true"), .Bits(4)) RAM (
    .A(pc_1_p3), .Din(4'b0000), .str(1'b0), .C(clk), .ld(1'b1), .D(RAM_d));
  ROM #(.Bits(2)) rom_1 (.A({and_1_out[0], register_1_q[0]}), .sel(1'b1), .D(pc_1_p2));
  Register #(.Bits(4)) IR (.D(RAM_d), .C(clk), .en(pc_1_p2[1]), .Q(IR_q));
  LookUpTable #(.Bits(9)) CU (.in0(IR_q[0]), .in1(IR_q[1]), .in2(IR_q[2]), .in3(IR_q[3]), .out(CU_out));
  Multiplexer #(.Bits(4)) multiplexer_1 (
    .sel(CU_out[3]), .in_0(multiplexer_2_out), .in_1(4'b0011), .out(multiplexer_1_out));
  register_file RF (
    .wdata(multiplexer_1_out), .rd(CU_out[5]), .wen(CU_out[4]), .rs1(CU_out[7]), .rs2(CU_out[6]), .clk(clk),
    .rdata1(RF_rdata1), .rdata2(RF_rdata2));
  // ALU alu_1: pin names not known; wires that end beside it: RF_rdata1, RF_rdata2, CU_out[2:0], alu_1_p4
  Multiplexer #(.Bits(4)) multiplexer_2 (.sel(CU_out[8]), .in_0(alu_1_p4), .in_1(RF_rdata1), .out(multiplexer_2_out));

  // Notes on the sheet:
  //   contents of rom_1 (hex, n*v repeats v):
  //   3
  //   contents of CU (hex, n*v repeats v):
  //   0,18,38,90,30,150,151,152,153,154,155
endmodule
